// Logisim project extensor_4 bits_para_8bits.circ as structural Verilog: 1 circuit, main circuit extensor
module extensor (
  input  [3:0] in_1,
  output [7:0] out_2
);


  assign out_2 = {4'b0000, in_1};
endmodule
