// Logisim project contador_sincrono.circ as structural Verilog: 2 circuits, main circuit cont_síncrono
module \cont_síncrono  (
  input  P,
  input  CLOCK,
  input  C,
  input  JK,
  output A3,
  output A2,
  output A4,
  output A1
);

  wire and_1_out, and_2_out;

  jk jk_1 (.j(and_1_out), .clk(CLOCK), .k(and_1_out), .p(P), .c(C), .Q(A4));  // open: out_7
  and and_1 (and_1_out, A3, and_2_out);
  jk jk_2 (.j(and_2_out), .clk(CLOCK), .k(and_2_out), .p(P), .c(C), .Q(A3));  // open: out_7
  and and_2 (and_2_out, A2, A1);
  jk jk_3 (.j(A1), .clk(CLOCK), .k(A1), .p(P), .c(C), .Q(A2));  // open: out_7
  jk jk_4 (.j(JK), .clk(CLOCK), .k(JK), .p(P), .c(C), .Q(A1));  // open: out_7
endmodule

module jk (
  input  p,
  input  j,
  input  clk,
  input  k,
  input  c,
  output Q,
  output out_7
);

  wire nand_1_out, nand_2_out, nand_3_out, nand_4_out, nand_5_out, nand_6_out, not_1_out;

  nand nand_1 (nand_1_out, j, clk, out_7);
  nand nand_2 (nand_2_out, Q, clk, k);
  not not_1 (not_1_out, clk);
  nand nand_3 (nand_3_out, p, nand_1_out, nand_4_out);
  nand nand_4 (nand_4_out, nand_3_out, nand_2_out, c);
  nand nand_5 (nand_5_out, not_1_out, nand_3_out);
  nand nand_6 (nand_6_out, nand_4_out, not_1_out);
  nand nand_7 (Q, p, nand_5_out, out_7);
  nand nand_8 (out_7, nand_6_out, Q, c);
endmodule
